// Logisim project 16BIT_ADDER.circ as structural Verilog: 2 circuits, main circuit CADDER_16BIT
module CADDER_16BIT (
  input  C,
  input  A0,
  input  B0,
  input  A1,
  input  B1,
  input  A2,
  input  B2,
  input  A3,
  input  B3,
  input  A4,
  input  B4,
  input  A5,
  input  B5,
  input  A6,
  input  B6,
  input  A7,
  input  B7,
  input  A8,
  input  B8,
  input  A9,
  input  B9,
  input  A10,
  input  B10,
  input  A11,
  input  B11,
  input  A12,
  input  B12,
  input  A13,
  input  B13,
  input  A14,
  input  B14,
  input  A15,
  input  B15,
  output S0,
  output S1,
  output S2,
  output S3,
  output S4,
  output S5,
  output S6,
  output S7,
  output S8,
  output S9,
  output S10,
  output S11,
  output S12,
  output S13,
  output S14,
  output S15,
  output Co
);

  wire and_1_out, and_2_out, and_3_out, and_4_out, and_5_out, and_6_out, and_7_out, and_8_out, and_9_out,
       and_10_out, and_11_out, and_12_out, and_13_out, and_14_out, and_15_out, and_16_out, and_17_out,
       and_18_out, and_19_out, and_20_out, and_21_out, and_22_out, and_23_out, and_24_out, and_25_out,
       and_26_out, and_27_out, and_28_out, and_29_out, and_30_out, and_31_out, and_32_out, or_1_out,
       or_2_out, or_3_out, or_4_out, or_5_out, or_6_out, or_7_out, or_8_out, or_9_out, or_10_out, or_11_out,
       or_12_out, or_13_out, or_14_out, or_15_out, xor_1_out, xor_2_out, xor_3_out, xor_4_out, xor_5_out,
       xor_6_out, xor_7_out, xor_8_out, xor_9_out, xor_10_out, xor_11_out, xor_12_out, xor_13_out,
       xor_14_out, xor_15_out, xor_16_out, xor_17_out, xor_18_out, xor_19_out, xor_20_out, xor_21_out,
       xor_22_out, xor_23_out, xor_24_out, xor_25_out, xor_26_out, xor_27_out, xor_28_out, xor_29_out,
       xor_30_out, xor_31_out, xor_32_out;

  xor xor_1 (xor_1_out, B0, A0);
  xor xor_2 (xor_2_out, C, B0);
  xor xor_3 (xor_3_out, B1, A1);
  xor xor_4 (xor_4_out, or_1_out, B1);
  xor xor_5 (xor_5_out, B2, A2);
  xor xor_6 (xor_6_out, or_2_out, B2);
  xor xor_7 (xor_7_out, B3, A3);
  xor xor_8 (xor_8_out, or_3_out, B3);
  xor xor_9 (xor_9_out, B4, A4);
  xor xor_10 (xor_10_out, or_4_out, B4);
  xor xor_11 (xor_11_out, B5, A5);
  xor xor_12 (xor_12_out, or_5_out, B5);
  xor xor_13 (xor_13_out, B6, A6);
  xor xor_14 (xor_14_out, or_6_out, B6);
  xor xor_15 (xor_15_out, B7, A7);
  xor xor_16 (xor_16_out, or_7_out, B7);
  xor xor_17 (xor_17_out, B8, A8);
  xor xor_18 (xor_18_out, or_8_out, B8);
  xor xor_19 (xor_19_out, B9, A9);
  xor xor_20 (xor_20_out, or_9_out, B9);
  xor xor_21 (xor_21_out, B10, A10);
  xor xor_22 (xor_22_out, or_10_out, B10);
  xor xor_23 (xor_23_out, B11, A11);
  xor xor_24 (xor_24_out, or_11_out, B11);
  xor xor_25 (xor_25_out, B12, A12);
  xor xor_26 (xor_26_out, or_12_out, B12);
  xor xor_27 (xor_27_out, B13, A13);
  xor xor_28 (xor_28_out, or_13_out, B13);
  xor xor_29 (xor_29_out, B14, A14);
  xor xor_30 (xor_30_out, or_14_out, B14);
  xor xor_31 (xor_31_out, B15, A15);
  xor xor_32 (xor_32_out, or_15_out, B15);
  and and_1 (and_1_out, C, B0);
  and and_2 (and_2_out, xor_2_out, A0);
  and and_3 (and_3_out, or_1_out, B1);
  and and_4 (and_4_out, xor_4_out, A1);
  and and_5 (and_5_out, or_2_out, B2);
  and and_6 (and_6_out, xor_6_out, A2);
  and and_7 (and_7_out, or_3_out, B3);
  and and_8 (and_8_out, xor_8_out, A3);
  and and_9 (and_9_out, or_4_out, B4);
  and and_10 (and_10_out, xor_10_out, A4);
  and and_11 (and_11_out, or_5_out, B5);
  and and_12 (and_12_out, xor_12_out, A5);
  and and_13 (and_13_out, or_6_out, B6);
  and and_14 (and_14_out, xor_14_out, A6);
  and and_15 (and_15_out, or_7_out, B7);
  and and_16 (and_16_out, xor_16_out, A7);
  and and_17 (and_17_out, or_8_out, B8);
  and and_18 (and_18_out, xor_18_out, A8);
  and and_19 (and_19_out, or_9_out, B9);
  and and_20 (and_20_out, xor_20_out, A9);
  and and_21 (and_21_out, or_10_out, B10);
  and and_22 (and_22_out, xor_22_out, A10);
  and and_23 (and_23_out, or_11_out, B11);
  and and_24 (and_24_out, xor_24_out, A11);
  and and_25 (and_25_out, or_12_out, B12);
  and and_26 (and_26_out, xor_26_out, A12);
  and and_27 (and_27_out, or_13_out, B13);
  and and_28 (and_28_out, xor_28_out, A13);
  and and_29 (and_29_out, or_14_out, B14);
  and and_30 (and_30_out, xor_30_out, A14);
  and and_31 (and_31_out, or_15_out, B15);
  and and_32 (and_32_out, xor_32_out, A15);
  xor xor_33 (S0, C, xor_1_out);
  or or_1 (or_1_out, and_1_out, and_2_out);
  xor xor_34 (S1, or_1_out, xor_3_out);
  or or_2 (or_2_out, and_3_out, and_4_out);
  xor xor_35 (S2, or_2_out, xor_5_out);
  or or_3 (or_3_out, and_5_out, and_6_out);
  xor xor_36 (S3, or_3_out, xor_7_out);
  or or_4 (or_4_out, and_7_out, and_8_out);
  xor xor_37 (S4, or_4_out, xor_9_out);
  or or_5 (or_5_out, and_9_out, and_10_out);
  xor xor_38 (S5, or_5_out, xor_11_out);
  or or_6 (or_6_out, and_11_out, and_12_out);
  xor xor_39 (S6, or_6_out, xor_13_out);
  or or_7 (or_7_out, and_13_out, and_14_out);
  xor xor_40 (S7, or_7_out, xor_15_out);
  or or_8 (or_8_out, and_15_out, and_16_out);
  xor xor_41 (S8, or_8_out, xor_17_out);
  or or_9 (or_9_out, and_17_out, and_18_out);
  xor xor_42 (S9, or_9_out, xor_19_out);
  or or_10 (or_10_out, and_19_out, and_20_out);
  xor xor_43 (S10, or_10_out, xor_21_out);
  or or_11 (or_11_out, and_21_out, and_22_out);
  xor xor_44 (S11, or_11_out, xor_23_out);
  or or_12 (or_12_out, and_23_out, and_24_out);
  xor xor_45 (S12, or_12_out, xor_25_out);
  or or_13 (or_13_out, and_25_out, and_26_out);
  xor xor_46 (S13, or_13_out, xor_27_out);
  or or_14 (or_14_out, and_27_out, and_28_out);
  xor xor_47 (S14, or_14_out, xor_29_out);
  or or_15 (or_15_out, and_29_out, and_30_out);
  xor xor_48 (S15, or_15_out, xor_31_out);
  or or_16 (Co, and_31_out, and_32_out);

  // Notes on the sheet:
  //   C
  //   C
  //   C
  //   C
  //   C
  //   C
  //   C
  //   C
  //   C
  //   C
  //   C
  //   C
  //   C
  //   C
  //   C
endmodule

module C16_ADDER (
);

  CADDER_16BIT cadder_16bit_1 ();  // open: C, A0, B0, A1, B1, A2, B2, A3, B3, A4, B4, A5, B5, A6, B6, A7, B7, A8, B8, A9, B9, A10, B10, A11, B11, A12, B12, A13, B13, A14, B14, A15, B15, S0, S1, S2, S3, S4, S5, S6, S7, S8, S9, S10, S11, S12, S13, S14, S15, Co
endmodule
