// Logisim project ACC_WITH_INCREMENT.circ as structural Verilog: 1 circuit, main circuit ACC
module ACC (
  input  L,
  input  INR,
  input  I_0,
  input  I_1,
  input  I_2,
  input  I_3,
  input  I_4,
  input  I_5,
  input  I_6,
  input  I_7,
  input  I_8,
  input  I_9,
  input  I_10,
  input  I_11,
  input  I_12,
  input  I_13,
  input  I_14,
  input  I_15,
  input  CLOCK,
  input  CLEAR,
  output D_0,
  output D_1,
  output D_2,
  output D_3,
  output D_4,
  output D_5,
  output D_6,
  output D_7,
  output D_8,
  output D_9,
  output D_10,
  output D_11,
  output D_12,
  output D_13,
  output D_14,
  output D_15
);

  wire and_1_out, and_2_out, and_3_out, and_4_out, and_5_out, and_6_out, and_7_out, and_8_out, and_9_out,
       and_10_out, and_11_out, and_12_out, and_13_out, and_14_out, and_15_out, and_16_out, and_17_out,
       and_18_out, and_19_out, and_20_out, and_21_out, and_22_out, and_23_out, and_24_out, and_25_out,
       and_26_out, and_27_out, and_28_out, and_29_out, and_30_out, and_31_out, and_32_out, d_ff_1_q,
       d_ff_2_q, d_ff_3_q, d_ff_4_q, d_ff_5_q, d_ff_6_q, d_ff_7_q, d_ff_8_q, d_ff_9_q, d_ff_10_q, d_ff_11_q,
       d_ff_12_q, d_ff_13_q, d_ff_14_q, d_ff_15_q, d_ff_16_q, halfadder_1_c, halfadder_2_c, halfadder_3_c,
       halfadder_4_c, halfadder_5_c, halfadder_6_c, halfadder_7_c, halfadder_8_c, halfadder_9_c,
       halfadder_10_c, halfadder_11_c, halfadder_12_c, halfadder_13_c, halfadder_14_c, halfadder_15_c,
       halfadder_16_c, not_1_out, or_1_out, or_2_out, or_3_out, or_4_out, or_5_out, or_6_out, or_7_out,
       or_8_out, or_9_out, or_10_out, or_11_out, or_12_out, or_13_out, or_14_out, or_15_out, or_16_out;

  not not_1 (not_1_out, L);
  and and_1 (and_1_out, D_0, not_1_out);
  and and_2 (and_2_out, L, I_0);
  and and_3 (and_3_out, D_1, not_1_out);
  and and_4 (and_4_out, L, I_1);
  and and_5 (and_5_out, D_2, not_1_out);
  and and_6 (and_6_out, L, I_2);
  and and_7 (and_7_out, D_3, not_1_out);
  and and_8 (and_8_out, L, I_3);
  and and_9 (and_9_out, D_4, not_1_out);
  and and_10 (and_10_out, L, I_4);
  and and_11 (and_11_out, D_5, not_1_out);
  and and_12 (and_12_out, L, I_5);
  and and_13 (and_13_out, D_6, not_1_out);
  and and_14 (and_14_out, L, I_6);
  and and_15 (and_15_out, D_7, not_1_out);
  and and_16 (and_16_out, L, I_7);
  and and_17 (and_17_out, D_8, not_1_out);
  and and_18 (and_18_out, L, I_8);
  and and_19 (and_19_out, D_9, not_1_out);
  and and_20 (and_20_out, L, I_9);
  and and_21 (and_21_out, D_10, not_1_out);
  and and_22 (and_22_out, L, I_10);
  and and_23 (and_23_out, D_11, not_1_out);
  and and_24 (and_24_out, L, I_11);
  and and_25 (and_25_out, D_12, not_1_out);
  and and_26 (and_26_out, L, I_12);
  and and_27 (and_27_out, D_13, not_1_out);
  and and_28 (and_28_out, L, I_13);
  and and_29 (and_29_out, D_14, not_1_out);
  and and_30 (and_30_out, L, I_14);
  and and_31 (and_31_out, D_15, not_1_out);
  and and_32 (and_32_out, L, I_15);
  D_Flip_Flop d_ff_1 (.D(or_1_out), .clk(CLOCK), .Q(d_ff_1_q), .reset(CLEAR));  // open: Qn, preset
  or or_1 (or_1_out, and_1_out, and_2_out);
  D_Flip_Flop d_ff_2 (.D(or_2_out), .clk(CLOCK), .Q(d_ff_2_q), .reset(CLEAR));  // open: Qn, preset
  or or_2 (or_2_out, and_3_out, and_4_out);
  D_Flip_Flop d_ff_3 (.D(or_3_out), .clk(CLOCK), .Q(d_ff_3_q), .reset(CLEAR));  // open: Qn, preset
  or or_3 (or_3_out, and_5_out, and_6_out);
  D_Flip_Flop d_ff_4 (.D(or_4_out), .clk(CLOCK), .Q(d_ff_4_q), .reset(CLEAR));  // open: Qn, preset
  or or_4 (or_4_out, and_7_out, and_8_out);
  D_Flip_Flop d_ff_5 (.D(or_5_out), .clk(CLOCK), .Q(d_ff_5_q), .reset(CLEAR));  // open: Qn, preset
  or or_5 (or_5_out, and_9_out, and_10_out);
  D_Flip_Flop d_ff_6 (.D(or_6_out), .clk(CLOCK), .Q(d_ff_6_q), .reset(CLEAR));  // open: Qn, preset
  or or_6 (or_6_out, and_11_out, and_12_out);
  D_Flip_Flop d_ff_7 (.D(or_7_out), .clk(CLOCK), .Q(d_ff_7_q), .reset(CLEAR));  // open: Qn, preset
  or or_7 (or_7_out, and_13_out, and_14_out);
  D_Flip_Flop d_ff_8 (.D(or_8_out), .clk(CLOCK), .Q(d_ff_8_q), .reset(CLEAR));  // open: Qn, preset
  or or_8 (or_8_out, and_15_out, and_16_out);
  D_Flip_Flop d_ff_9 (.D(or_9_out), .clk(CLOCK), .Q(d_ff_9_q), .reset(CLEAR));  // open: Qn, preset
  or or_9 (or_9_out, and_17_out, and_18_out);
  D_Flip_Flop d_ff_10 (.D(or_10_out), .clk(CLOCK), .Q(d_ff_10_q), .reset(CLEAR));  // open: Qn, preset
  or or_10 (or_10_out, and_19_out, and_20_out);
  D_Flip_Flop d_ff_11 (.D(or_11_out), .clk(CLOCK), .Q(d_ff_11_q), .reset(CLEAR));  // open: Qn, preset
  or or_11 (or_11_out, and_21_out, and_22_out);
  D_Flip_Flop d_ff_12 (.D(or_12_out), .clk(CLOCK), .Q(d_ff_12_q), .reset(CLEAR));  // open: Qn, preset
  or or_12 (or_12_out, and_23_out, and_24_out);
  D_Flip_Flop d_ff_13 (.D(or_13_out), .clk(CLOCK), .Q(d_ff_13_q), .reset(CLEAR));  // open: Qn, preset
  or or_13 (or_13_out, and_25_out, and_26_out);
  D_Flip_Flop d_ff_14 (.D(or_14_out), .clk(CLOCK), .Q(d_ff_14_q), .reset(CLEAR));  // open: Qn, preset
  or or_14 (or_14_out, and_27_out, and_28_out);
  D_Flip_Flop d_ff_15 (.D(or_15_out), .clk(CLOCK), .Q(d_ff_15_q), .reset(CLEAR));  // open: Qn, preset
  or or_15 (or_15_out, and_29_out, and_30_out);
  D_Flip_Flop d_ff_16 (.D(or_16_out), .clk(CLOCK), .Q(d_ff_16_q), .reset(CLEAR));  // open: Qn, preset
  or or_16 (or_16_out, and_31_out, and_32_out);
  HalfAdder halfadder_1 (.A(d_ff_1_q), .B(INR), .S(D_0), .C(halfadder_1_c));
  HalfAdder halfadder_2 (.A(d_ff_2_q), .B(halfadder_1_c), .S(D_1), .C(halfadder_2_c));
  HalfAdder halfadder_3 (.A(d_ff_3_q), .B(halfadder_2_c), .S(D_2), .C(halfadder_3_c));
  HalfAdder halfadder_4 (.A(d_ff_4_q), .B(halfadder_3_c), .S(D_3), .C(halfadder_4_c));
  HalfAdder halfadder_5 (.A(d_ff_5_q), .B(halfadder_4_c), .S(D_4), .C(halfadder_5_c));
  HalfAdder halfadder_6 (.A(d_ff_6_q), .B(halfadder_5_c), .S(D_5), .C(halfadder_6_c));
  HalfAdder halfadder_7 (.A(d_ff_7_q), .B(halfadder_6_c), .S(D_6), .C(halfadder_7_c));
  HalfAdder halfadder_8 (.A(d_ff_8_q), .B(halfadder_7_c), .S(D_7), .C(halfadder_8_c));
  HalfAdder halfadder_9 (.A(d_ff_9_q), .B(halfadder_8_c), .S(D_8), .C(halfadder_9_c));
  HalfAdder halfadder_10 (.A(d_ff_10_q), .B(halfadder_9_c), .S(D_9), .C(halfadder_10_c));
  HalfAdder halfadder_11 (.A(d_ff_11_q), .B(halfadder_10_c), .S(D_10), .C(halfadder_11_c));
  HalfAdder halfadder_12 (.A(d_ff_12_q), .B(halfadder_11_c), .S(D_11), .C(halfadder_12_c));
  HalfAdder halfadder_13 (.A(d_ff_13_q), .B(halfadder_12_c), .S(D_12), .C(halfadder_13_c));
  HalfAdder halfadder_14 (.A(d_ff_14_q), .B(halfadder_13_c), .S(D_13), .C(halfadder_14_c));
  HalfAdder halfadder_15 (.A(d_ff_15_q), .B(halfadder_14_c), .S(D_14), .C(halfadder_15_c));
  HalfAdder halfadder_16 (.A(d_ff_16_q), .B(halfadder_15_c), .S(D_15), .C(halfadder_16_c));
endmodule
