// Logisim project ALU_MAIN.circ as structural Verilog: 1 circuit, main circuit ALU_16
module ALU_16 (
  input  S_3,
  input  S_2,
  input  S_1,
  input  S_0,
  input  C,
  input  A_0,
  input  A_1,
  input  A_2,
  input  A_3,
  input  A_4,
  input  A_5,
  input  A_6,
  input  A_7,
  input  A_8,
  input  A_9,
  input  A_10,
  input  A_11,
  input  A_12,
  input  A_13,
  input  A_14,
  input  A_15,
  input  B_0,
  input  B_1,
  input  B_2,
  input  B_3,
  input  B_4,
  input  B_5,
  input  B_6,
  input  B_7,
  input  B_8,
  input  B_9,
  input  B_10,
  input  B_11,
  input  B_12,
  input  B_13,
  input  B_14,
  input  B_15,
  output F_0,
  output F_1,
  output F_2,
  output F_3,
  output F_4,
  output F_5,
  output F_6,
  output F_7,
  output F_8,
  output F_9,
  output F_10,
  output F_11,
  output F_12,
  output F_13,
  output F_14,
  output F_15,
  output C0
);

  wire arithmetic_16_1_p18, arithmetic_16_1_p19, arithmetic_16_1_p20, arithmetic_16_1_p21,
       arithmetic_16_1_p22, arithmetic_16_1_p23, arithmetic_16_1_p24, arithmetic_16_1_p25,
       arithmetic_16_1_p26, arithmetic_16_1_p27, arithmetic_16_1_p28, arithmetic_16_1_p29,
       arithmetic_16_1_p30, arithmetic_16_1_p31, arithmetic_16_1_p32, arithmetic_16_1_p33,
       arithmetic_16_1_p34, logic_16_1_p32, logic_16_1_p33, logic_16_1_p34, logic_16_1_p35, logic_16_1_p36,
       logic_16_1_p37, logic_16_1_p38, logic_16_1_p39, logic_16_1_p40, logic_16_1_p41, logic_16_1_p42,
       logic_16_1_p43, logic_16_1_p44, logic_16_1_p45, logic_16_1_p46, logic_16_1_p47;

  // ARITHMETIC_16 arithmetic_16_1: pin names not known; wires that end beside it: S_1, S_0, C, A_0, A_1, A_2, A_3, A_4, A_5, A_6, A_7, A_8, A_9, A_10, A_11, A_12, A_13, arithmetic_16_1_p18, arithmetic_16_1_p19, arithmetic_16_1_p20, arithmetic_16_1_p21, arithmetic_16_1_p22, arithmetic_16_1_p23, arithmetic_16_1_p24, arithmetic_16_1_p25, arithmetic_16_1_p26, arithmetic_16_1_p27, arithmetic_16_1_p28, arithmetic_16_1_p29, arithmetic_16_1_p30, arithmetic_16_1_p31, arithmetic_16_1_p32, arithmetic_16_1_p33, arithmetic_16_1_p34
  // LOGIC_16 logic_16_1: pin names not known; wires that end beside it: B_2, B_3, B_4, B_5, B_6, B_7, B_8, B_9, B_10, B_11, B_12, B_13, B_14, B_15, S_1, S_0, A_0, A_1, A_2, A_3, A_4, A_5, A_6, A_7, A_8, A_9, A_10, A_11, A_12, A_13, A_14, logic_16_1_p32, logic_16_1_p33, logic_16_1_p34, logic_16_1_p35, logic_16_1_p36, logic_16_1_p37, logic_16_1_p38, logic_16_1_p39, logic_16_1_p40, logic_16_1_p41, logic_16_1_p42, logic_16_1_p43, logic_16_1_p44, logic_16_1_p45, logic_16_1_p46, logic_16_1_p47
  // SMULTIPLEXER4x1 smultiplexer4x1_1: pin names not known; wires that end beside it: S_3, S_2, arithmetic_16_1_p18, logic_16_1_p32, F_0
  // SMULTIPLEXER4x1 smultiplexer4x1_2: pin names not known; wires that end beside it: arithmetic_16_1_p18, arithmetic_16_1_p19, S_3, S_2, arithmetic_16_1_p19, logic_16_1_p33, F_1
  // SMULTIPLEXER4x1 smultiplexer4x1_3: pin names not known; wires that end beside it: arithmetic_16_1_p18, arithmetic_16_1_p20, S_3, S_2, arithmetic_16_1_p20, logic_16_1_p34, F_2
  // SMULTIPLEXER4x1 smultiplexer4x1_4: pin names not known; wires that end beside it: arithmetic_16_1_p19, arithmetic_16_1_p21, S_3, S_2, arithmetic_16_1_p21, logic_16_1_p35, F_3
  // SMULTIPLEXER4x1 smultiplexer4x1_5: pin names not known; wires that end beside it: arithmetic_16_1_p20, arithmetic_16_1_p22, S_3, S_2, arithmetic_16_1_p22, logic_16_1_p36, F_4
  // SMULTIPLEXER4x1 smultiplexer4x1_6: pin names not known; wires that end beside it: arithmetic_16_1_p21, arithmetic_16_1_p23, S_3, S_2, arithmetic_16_1_p23, logic_16_1_p37, F_5
  // SMULTIPLEXER4x1 smultiplexer4x1_7: pin names not known; wires that end beside it: arithmetic_16_1_p22, arithmetic_16_1_p24, S_3, S_2, arithmetic_16_1_p24, logic_16_1_p38, F_6
  // SMULTIPLEXER4x1 smultiplexer4x1_8: pin names not known; wires that end beside it: arithmetic_16_1_p23, arithmetic_16_1_p25, S_3, S_2, arithmetic_16_1_p25, logic_16_1_p39, F_7
  // SMULTIPLEXER4x1 smultiplexer4x1_9: pin names not known; wires that end beside it: arithmetic_16_1_p24, arithmetic_16_1_p26, S_3, S_2, arithmetic_16_1_p26, logic_16_1_p40, F_8
  // SMULTIPLEXER4x1 smultiplexer4x1_10: pin names not known; wires that end beside it: arithmetic_16_1_p25, arithmetic_16_1_p27, S_3, S_2, arithmetic_16_1_p27, logic_16_1_p41, F_9
  // SMULTIPLEXER4x1 smultiplexer4x1_11: pin names not known; wires that end beside it: arithmetic_16_1_p26, arithmetic_16_1_p28, S_3, S_2, arithmetic_16_1_p28, logic_16_1_p42, F_10
  // SMULTIPLEXER4x1 smultiplexer4x1_12: pin names not known; wires that end beside it: arithmetic_16_1_p27, arithmetic_16_1_p29, S_3, S_2, arithmetic_16_1_p29, logic_16_1_p43, F_11
  // SMULTIPLEXER4x1 smultiplexer4x1_13: pin names not known; wires that end beside it: arithmetic_16_1_p28, arithmetic_16_1_p30, S_3, S_2, arithmetic_16_1_p30, logic_16_1_p44, F_12
  // SMULTIPLEXER4x1 smultiplexer4x1_14: pin names not known; wires that end beside it: arithmetic_16_1_p29, arithmetic_16_1_p31, S_3, S_2, arithmetic_16_1_p31, logic_16_1_p45, F_13
  // SMULTIPLEXER4x1 smultiplexer4x1_15: pin names not known; wires that end beside it: arithmetic_16_1_p30, arithmetic_16_1_p32, S_3, S_2, arithmetic_16_1_p32, logic_16_1_p46, F_14
  // SMULTIPLEXER4x1 smultiplexer4x1_16: pin names not known; wires that end beside it: arithmetic_16_1_p31, arithmetic_16_1_p33, S_3, S_2, arithmetic_16_1_p33, logic_16_1_p47, F_15
  // SMULTIPLEXER4x1 smultiplexer4x1_17: pin names not known; wires that end beside it: arithmetic_16_1_p32, arithmetic_16_1_p33, S_3, S_2, arithmetic_16_1_p34, arithmetic_16_1_p34, arithmetic_16_1_p33, arithmetic_16_1_p18, C0
endmodule
