// Logisim project CB8x1_Multiplexer.circ as structural Verilog: 1 circuit, main circuit CBMUX8x1
module CBMUX8x1 (
  input  S_2,
  input  S_1,
  input  S_0,
  input  I_0,
  input  I_1,
  input  I_2,
  input  I_3,
  input  I_4,
  input  I_5,
  input  I_6,
  input  I_7,
  output O
);

  wire and_1_out, and_2_out, and_3_out, and_4_out, and_5_out, and_6_out, and_7_out, and_8_out, and_9_out,
       and_10_out, not_1_out, not_2_out, not_3_out, or_1_out, or_2_out;

  not not_1 (not_1_out, S_2);
  not not_2 (not_2_out, S_1);
  not not_3 (not_3_out, S_0);
  and and_1 (and_1_out, not_2_out, not_3_out, I_0);
  and and_2 (and_2_out, not_2_out, S_0, I_1);
  and and_3 (and_3_out, S_1, not_3_out, I_2);
  and and_4 (and_4_out, S_1, S_0, I_3);
  and and_5 (and_5_out, not_2_out, not_3_out, I_4);
  and and_6 (and_6_out, not_2_out, S_0, I_5);
  and and_7 (and_7_out, S_1, not_3_out, I_6);
  and and_8 (and_8_out, S_1, S_0, I_7);
  or or_1 (or_1_out, and_1_out, and_2_out, and_3_out, and_4_out);
  or or_2 (or_2_out, and_5_out, and_6_out, and_7_out, and_8_out);
  and and_9 (and_9_out, not_1_out, or_1_out);
  and and_10 (and_10_out, S_2, or_2_out);
  or or_3 (O, and_9_out, and_10_out);
endmodule
