// Logisim project CDecoder3x8.circ as structural Verilog
module Decoder3x8 (
  input  X,
  input  Y,
  input  Z,
  input  E,
  output out_5,
  output out_6,
  output out_7,
  output out_8,
  output out_9,
  output out_10,
  output out_11,
  output out_12
);

  wire not_1_out, not_2_out, not_3_out;

  not not_1 (not_1_out, X);
  not not_2 (not_2_out, Y);
  not not_3 (not_3_out, Z);
  and and_1 (out_5, not_1_out, not_2_out, not_3_out, E);
  and and_2 (out_6, not_1_out, not_2_out, Z, E);
  and and_3 (out_7, not_1_out, Y, not_3_out, E);
  and and_4 (out_8, not_1_out, Y, Z, E);
  and and_5 (out_9, X, not_2_out, not_3_out, E);
  and and_6 (out_10, X, not_2_out, Z, E);
  and and_7 (out_11, X, Y, not_3_out, E);
  and and_8 (out_12, X, Y, Z, E);
endmodule
