// Logisim project Common_Bus_16BIT.circ as structural Verilog: 1 circuit, main circuit COMMON_BUS_16
module COMMON_BUS_16 (
  input  S_2,
  input  S_1,
  input  S_0,
  input  A_0,
  input  A_1,
  input  A_2,
  input  A_3,
  input  A_4,
  input  A_5,
  input  A_6,
  input  A_7,
  input  A_8,
  input  A_9,
  input  A_10,
  input  A_11,
  input  A_12,
  input  A_13,
  input  A_14,
  input  A_15,
  input  B_0,
  input  B_1,
  input  B_2,
  input  B_3,
  input  B_4,
  input  B_5,
  input  B_6,
  input  B_7,
  input  B_8,
  input  B_9,
  input  B_10,
  input  B_11,
  input  B_12,
  input  B_13,
  input  B_14,
  input  B_15,
  input  C_0,
  input  C_1,
  input  C_2,
  input  C_3,
  input  C_4,
  input  C_5,
  input  C_6,
  input  C_7,
  input  C_8,
  input  C_9,
  input  C_10,
  input  C_11,
  input  C_12,
  input  C_13,
  input  C_14,
  input  C_15,
  input  D_0,
  input  D_1,
  input  D_2,
  input  D_3,
  input  D_4,
  input  D_5,
  input  D_6,
  input  D_7,
  input  D_8,
  input  D_9,
  input  D_10,
  input  D_11,
  input  D_12,
  input  D_13,
  input  D_14,
  input  D_15,
  input  E_0,
  input  E_1,
  input  E_2,
  input  E_3,
  input  E_4,
  input  E_5,
  input  E_6,
  input  E_7,
  input  E_8,
  input  E_9,
  input  E_10,
  input  E_11,
  input  E_12,
  input  E_13,
  input  E_14,
  input  E_15,
  input  F_0,
  input  F_1,
  input  F_2,
  input  F_3,
  input  F_4,
  input  F_5,
  input  F_6,
  input  F_7,
  input  F_8,
  input  F_9,
  input  F_10,
  input  F_11,
  input  F_12,
  input  F_13,
  input  F_14,
  input  F_15,
  input  G_0,
  input  G_1,
  input  G_2,
  input  G_3,
  input  G_4,
  input  G_5,
  input  G_6,
  input  G_7,
  input  G_8,
  input  G_9,
  input  G_10,
  input  G_11,
  input  G_12,
  input  G_13,
  input  G_14,
  input  G_15,
  input  H_0,
  input  H_1,
  input  H_2,
  input  H_3,
  input  H_4,
  input  H_5,
  input  H_6,
  input  H_7,
  input  H_8,
  input  H_9,
  input  H_10,
  input  H_11,
  input  H_12,
  input  H_13,
  input  H_14,
  input  H_15,
  output DATA_0,
  output DATA_1,
  output DATA_2,
  output DATA_3,
  output DATA_4,
  output DATA_5,
  output DATA_6,
  output DATA_7,
  output DATA_8,
  output DATA_9,
  output DATA_10,
  output DATA_11,
  output DATA_12,
  output DATA_13,
  output DATA_14,
  output DATA_15
);

  CBMUX8x1 cbmux8x1_1 (
    .S_2(S_2), .S_1(S_1), .S_0(S_0), .I_0(A_0), .I_1(B_0), .I_2(C_0), .I_3(D_0), .I_4(E_0), .I_5(F_0),
    .I_6(G_0), .I_7(H_0), .O(DATA_0));
  CBMUX8x1 cbmux8x1_2 (
    .S_2(S_2), .S_1(S_1), .S_0(S_0), .I_0(A_1), .I_1(B_1), .I_2(C_1), .I_3(D_1), .I_4(E_1), .I_5(F_1),
    .I_6(G_1), .I_7(H_1), .O(DATA_1));
  CBMUX8x1 cbmux8x1_3 (
    .S_2(S_2), .S_1(S_1), .S_0(S_0), .I_0(A_2), .I_1(B_2), .I_2(C_2), .I_3(D_2), .I_4(E_2), .I_5(F_2),
    .I_6(G_2), .I_7(H_2), .O(DATA_2));
  CBMUX8x1 cbmux8x1_4 (
    .S_2(S_2), .S_1(S_1), .S_0(S_0), .I_0(A_3), .I_1(B_3), .I_2(C_3), .I_3(D_3), .I_4(E_3), .I_5(F_3),
    .I_6(G_3), .I_7(H_3), .O(DATA_3));
  CBMUX8x1 cbmux8x1_5 (
    .S_2(S_2), .S_1(S_1), .S_0(S_0), .I_0(A_4), .I_1(B_4), .I_2(C_4), .I_3(D_4), .I_4(E_4), .I_5(F_4),
    .I_6(G_4), .I_7(H_4), .O(DATA_4));
  CBMUX8x1 cbmux8x1_6 (
    .S_2(S_2), .S_1(S_1), .S_0(S_0), .I_0(A_5), .I_1(B_5), .I_2(C_5), .I_3(D_5), .I_4(E_5), .I_5(F_5),
    .I_6(G_5), .I_7(H_5), .O(DATA_5));
  CBMUX8x1 cbmux8x1_7 (
    .S_2(S_2), .S_1(S_1), .S_0(S_0), .I_0(A_6), .I_1(B_6), .I_2(C_6), .I_3(D_6), .I_4(E_6), .I_5(F_6),
    .I_6(G_6), .I_7(H_6), .O(DATA_6));
  CBMUX8x1 cbmux8x1_8 (
    .S_2(S_2), .S_1(S_1), .S_0(S_0), .I_0(A_7), .I_1(B_7), .I_2(C_7), .I_3(D_7), .I_4(E_7), .I_5(F_7),
    .I_6(G_7), .I_7(H_7), .O(DATA_7));
  CBMUX8x1 cbmux8x1_9 (
    .S_2(S_2), .S_1(S_1), .S_0(S_0), .I_0(A_8), .I_1(B_8), .I_2(C_8), .I_3(D_8), .I_4(E_8), .I_5(F_8),
    .I_6(G_8), .I_7(H_8), .O(DATA_8));
  CBMUX8x1 cbmux8x1_10 (
    .S_2(S_2), .S_1(S_1), .S_0(S_0), .I_0(A_9), .I_1(B_9), .I_2(C_9), .I_3(D_9), .I_4(E_9), .I_5(F_9),
    .I_6(G_9), .I_7(H_9), .O(DATA_9));
  CBMUX8x1 cbmux8x1_11 (
    .S_2(S_2), .S_1(S_1), .S_0(S_0), .I_0(A_10), .I_1(B_10), .I_2(C_10), .I_3(D_10), .I_4(E_10), .I_5(F_10),
    .I_6(G_10), .I_7(H_10), .O(DATA_10));
  CBMUX8x1 cbmux8x1_12 (
    .S_2(S_2), .S_1(S_1), .S_0(S_0), .I_0(A_11), .I_1(B_11), .I_2(C_11), .I_3(D_11), .I_4(E_11), .I_5(F_11),
    .I_6(G_11), .I_7(H_11), .O(DATA_11));
  CBMUX8x1 cbmux8x1_13 (
    .S_2(S_2), .S_1(S_1), .S_0(S_0), .I_0(A_12), .I_1(B_12), .I_2(C_12), .I_3(D_12), .I_4(E_12), .I_5(F_12),
    .I_6(G_12), .I_7(H_12), .O(DATA_12));
  CBMUX8x1 cbmux8x1_14 (
    .S_2(S_2), .S_1(S_1), .S_0(S_0), .I_0(A_13), .I_1(B_13), .I_2(C_13), .I_3(D_13), .I_4(E_13), .I_5(F_13),
    .I_6(G_13), .I_7(H_13), .O(DATA_13));
  CBMUX8x1 cbmux8x1_15 (
    .S_2(S_2), .S_1(S_1), .S_0(S_0), .I_0(A_14), .I_1(B_14), .I_2(C_14), .I_3(D_14), .I_4(E_14), .I_5(F_14),
    .I_6(G_14), .I_7(H_14), .O(DATA_14));
  CBMUX8x1 cbmux8x1_16 (
    .S_2(S_2), .S_1(S_1), .S_0(S_0), .I_0(A_15), .I_1(B_15), .I_2(C_15), .I_3(D_15), .I_4(E_15), .I_5(F_15),
    .I_6(G_15), .I_7(H_15), .O(DATA_15));
endmodule
