// Logisim project FullAdder.circ as structural Verilog: 1 circuit, main circuit main
module main (
  input  C,
  input  B0,
  input  A0,
  output S0
);

  wire and_1_out, and_2_out, or_1_out, xor_1_out, xor_2_out;

  xor xor_1 (xor_1_out, B0, A0);
  xor xor_2 (xor_2_out, C, B0);
  and and_1 (and_1_out, C, B0);
  and and_2 (and_2_out, xor_2_out, A0);
  xor xor_3 (S0, C, xor_1_out);
  or or_1 (or_1_out, and_1_out, and_2_out);
  LED led_1 (.in(or_1_out));

  // Notes on the sheet:
  //   Co
endmodule
