// Logisim project RAM_4Byte.circ as structural Verilog: 1 circuit, main circuit main
module main (
);

  wire multiplexer4x1_1_p1, multiplexer4x1_2_p1, multiplexer4x1_3_p1, multiplexer4x1_4_p1,
       multiplexer4x1_5_p1, multiplexer4x1_6_p1, multiplexer4x1_7_p1, multiplexer4x1_8_p1, undriven_2,
       undriven_3, undriven_4, undriven_5;
  wire [7:0] d_ff_29_q, d_ff_30_q, d_ff_31_q, d_ff_32_q, undriven;

  D_Flip_Flop d_ff_1 (.D(undriven[7]), .Q(d_ff_29_q[7]), .reset(undriven_2));  // open: clk, Qn, preset
  D_Flip_Flop d_ff_2 (.D(undriven[7]), .Q(d_ff_30_q[7]), .reset(undriven_3));  // open: clk, Qn, preset
  D_Flip_Flop d_ff_3 (.D(undriven[7]), .Q(d_ff_31_q[7]), .reset(undriven_4));  // open: clk, Qn, preset
  D_Flip_Flop d_ff_4 (.D(undriven[7]), .Q(d_ff_32_q[7]), .reset(undriven_5));  // open: clk, Qn, preset
  D_Flip_Flop d_ff_5 (.D(undriven[6]), .Q(d_ff_29_q[6]), .reset(undriven_2));  // open: clk, Qn, preset
  D_Flip_Flop d_ff_6 (.D(undriven[6]), .Q(d_ff_30_q[6]), .reset(undriven_3));  // open: clk, Qn, preset
  D_Flip_Flop d_ff_7 (.D(undriven[6]), .Q(d_ff_31_q[6]), .reset(undriven_4));  // open: clk, Qn, preset
  D_Flip_Flop d_ff_8 (.D(undriven[6]), .Q(d_ff_32_q[6]), .reset(undriven_5));  // open: clk, Qn, preset
  D_Flip_Flop d_ff_9 (.D(undriven[5]), .Q(d_ff_29_q[5]), .reset(undriven_2));  // open: clk, Qn, preset
  D_Flip_Flop d_ff_10 (.D(undriven[5]), .Q(d_ff_30_q[5]), .reset(undriven_3));  // open: clk, Qn, preset
  D_Flip_Flop d_ff_11 (.D(undriven[5]), .Q(d_ff_31_q[5]), .reset(undriven_4));  // open: clk, Qn, preset
  D_Flip_Flop d_ff_12 (.D(undriven[5]), .Q(d_ff_32_q[5]), .reset(undriven_5));  // open: clk, Qn, preset
  D_Flip_Flop d_ff_13 (.D(undriven[4]), .Q(d_ff_29_q[4]), .reset(undriven_2));  // open: clk, Qn, preset
  D_Flip_Flop d_ff_14 (.D(undriven[4]), .Q(d_ff_30_q[4]), .reset(undriven_3));  // open: clk, Qn, preset
  D_Flip_Flop d_ff_15 (.D(undriven[4]), .Q(d_ff_31_q[4]), .reset(undriven_4));  // open: clk, Qn, preset
  D_Flip_Flop d_ff_16 (.D(undriven[4]), .Q(d_ff_32_q[4]), .reset(undriven_5));  // open: clk, Qn, preset
  D_Flip_Flop d_ff_17 (.D(undriven[3]), .Q(d_ff_29_q[3]), .reset(undriven_2));  // open: clk, Qn, preset
  D_Flip_Flop d_ff_18 (.D(undriven[3]), .Q(d_ff_30_q[3]), .reset(undriven_3));  // open: clk, Qn, preset
  D_Flip_Flop d_ff_19 (.D(undriven[3]), .Q(d_ff_31_q[3]), .reset(undriven_4));  // open: clk, Qn, preset
  D_Flip_Flop d_ff_20 (.D(undriven[3]), .Q(d_ff_32_q[3]), .reset(undriven_5));  // open: clk, Qn, preset
  D_Flip_Flop d_ff_21 (.D(undriven[2]), .Q(d_ff_29_q[2]), .reset(undriven_2));  // open: clk, Qn, preset
  D_Flip_Flop d_ff_22 (.D(undriven[2]), .Q(d_ff_30_q[2]), .reset(undriven_3));  // open: clk, Qn, preset
  D_Flip_Flop d_ff_23 (.D(undriven[2]), .Q(d_ff_31_q[2]), .reset(undriven_4));  // open: clk, Qn, preset
  D_Flip_Flop d_ff_24 (.D(undriven[2]), .Q(d_ff_32_q[2]), .reset(undriven_5));  // open: clk, Qn, preset
  D_Flip_Flop d_ff_25 (.D(undriven[1]), .Q(d_ff_29_q[1]), .reset(undriven_2));  // open: clk, Qn, preset
  D_Flip_Flop d_ff_26 (.D(undriven[1]), .Q(d_ff_30_q[1]), .reset(undriven_3));  // open: clk, Qn, preset
  D_Flip_Flop d_ff_27 (.D(undriven[1]), .Q(d_ff_31_q[1]), .reset(undriven_4));  // open: clk, Qn, preset
  D_Flip_Flop d_ff_28 (.D(undriven[1]), .Q(d_ff_32_q[1]), .reset(undriven_5));  // open: clk, Qn, preset
  D_Flip_Flop d_ff_29 (.D(undriven[0]), .Q(d_ff_29_q[0]), .reset(undriven_2));  // open: clk, Qn, preset
  D_Flip_Flop d_ff_30 (.D(undriven[0]), .Q(d_ff_30_q[0]), .reset(undriven_3));  // open: clk, Qn, preset
  D_Flip_Flop d_ff_31 (.D(undriven[0]), .Q(d_ff_31_q[0]), .reset(undriven_4));  // open: clk, Qn, preset
  D_Flip_Flop d_ff_32 (.D(undriven[0]), .Q(d_ff_32_q[0]), .reset(undriven_5));  // open: clk, Qn, preset
  // MULTIPLEXER4x1 multiplexer4x1_1: pin names not known; wires that end beside it: multiplexer4x1_1_p1
  // MULTIPLEXER4x1 multiplexer4x1_2: pin names not known; wires that end beside it: multiplexer4x1_2_p1
  // MULTIPLEXER4x1 multiplexer4x1_3: pin names not known; wires that end beside it: multiplexer4x1_3_p1
  // MULTIPLEXER4x1 multiplexer4x1_4: pin names not known; wires that end beside it: multiplexer4x1_4_p1
  // MULTIPLEXER4x1 multiplexer4x1_5: pin names not known; wires that end beside it: multiplexer4x1_5_p1
  // MULTIPLEXER4x1 multiplexer4x1_6: pin names not known; wires that end beside it: multiplexer4x1_6_p1
  // MULTIPLEXER4x1 multiplexer4x1_7: pin names not known; wires that end beside it: multiplexer4x1_7_p1
  // MULTIPLEXER4x1 multiplexer4x1_8: pin names not known; wires that end beside it: multiplexer4x1_8_p1
  LED led_1 (.in(multiplexer4x1_1_p1));
  LED led_2 (.in(multiplexer4x1_2_p1));
  LED led_3 (.in(multiplexer4x1_3_p1));
  LED led_4 (.in(multiplexer4x1_4_p1));
  LED led_5 (.in(multiplexer4x1_5_p1));
  LED led_6 (.in(multiplexer4x1_6_p1));
  LED led_7 (.in(multiplexer4x1_7_p1));
  LED led_8 (.in(multiplexer4x1_8_p1));
endmodule
