// Logisim project SR_FlipFlop.circ as structural Verilog: 1 circuit, main circuit SRFLIPFLOP
module SRFLIPFLOP (
  input  S,
  input  C,
  input  R,
  output Q,
  output Q1
);

  wire nand_1_out, nand_2_out;

  nand nand_1 (nand_1_out, S, C);
  nand nand_2 (nand_2_out, C, R);
  nand nand_3 (Q, nand_1_out, Q1);
  nand nand_4 (Q1, Q, nand_2_out);
endmodule
