// Logisim project TCounter.circ as structural Verilog: 2 circuits, main circuit main
module main (
  input  C,
  input  CLEAR,
  output out_3,
  output out_4,
  output out_5,
  output out_6
);

  wire and_1_out, and_2_out;

  T_Flip_Flop t_ff_1 (.T(and_1_out), .clk(C), .Q(out_3), .reset(CLEAR));  // open: Qn, preset
  T_Flip_Flop t_ff_2 (.T(and_2_out), .clk(C), .Q(out_4), .reset(CLEAR));  // open: Qn, preset
  T_Flip_Flop t_ff_3 (.T(out_6), .clk(C), .Q(out_5), .reset(CLEAR));  // open: Qn, preset
  T_Flip_Flop t_ff_4 (.T(1'b1), .clk(C), .Q(out_6), .reset(CLEAR));  // open: Qn, preset
  and and_1 (and_1_out, out_4, out_5, out_6);
  and and_2 (and_2_out, out_5, out_6);
endmodule

module COUNTER_4BIT (
  input  in_1,
  output out_2,
  output out_3,
  output out_4,
  output out_5
);

  wire clock_1_out;

  Clock clock_1 (.out(clock_1_out));
  main main_1 (.C(clock_1_out), .CLEAR(in_1), .out_3(out_2), .out_4(out_3), .out_5(out_4), .out_6(out_5));
endmodule
