// Logisim project using_splitter.circ as structural Verilog: 1 circuit, main circuit main
module main (
);

  wire [3:0] common_bus_16_1_data_12, pc_1_p2;
  wire [7:0] ar_1_p1, undriven_4;
  wire [11:0] undriven, undriven_2;
  wire [15:0] alu_16_1_f_0, dr_1_p1, ir_1_p1, ram_1_dout, tr_1_p6, undriven_3;

  ALU_16 alu_16_1 (
    .A_0(ar_1_p1[0]), .A_1(ar_1_p1[1]), .A_2(ar_1_p1[2]), .A_3(ar_1_p1[3]), .A_4(ar_1_p1[4]),
    .A_5(ar_1_p1[5]), .A_6(ar_1_p1[6]), .A_7(ar_1_p1[7]), .A_8(pc_1_p2[0]), .A_9(pc_1_p2[1]),
    .A_10(pc_1_p2[2]), .A_11(pc_1_p2[3]), .A_12(common_bus_16_1_data_12[0]),
    .A_13(common_bus_16_1_data_12[1]), .A_14(common_bus_16_1_data_12[2]), .A_15(common_bus_16_1_data_12[3]),
    .B_0(dr_1_p1[0]), .B_1(dr_1_p1[1]), .B_2(dr_1_p1[2]), .B_3(dr_1_p1[3]), .B_4(dr_1_p1[4]),
    .B_5(dr_1_p1[5]), .B_6(dr_1_p1[6]), .B_7(dr_1_p1[7]), .B_8(dr_1_p1[8]), .B_9(dr_1_p1[9]),
    .B_10(dr_1_p1[10]), .B_11(dr_1_p1[11]), .B_12(dr_1_p1[12]), .B_13(dr_1_p1[13]), .B_14(dr_1_p1[14]),
    .B_15(dr_1_p1[15]), .F_0(alu_16_1_f_0[0]), .F_1(alu_16_1_f_0[1]), .F_2(alu_16_1_f_0[2]),
    .F_3(alu_16_1_f_0[3]), .F_4(alu_16_1_f_0[4]), .F_5(alu_16_1_f_0[5]), .F_6(alu_16_1_f_0[6]),
    .F_7(alu_16_1_f_0[7]), .F_8(alu_16_1_f_0[8]), .F_9(alu_16_1_f_0[9]), .F_10(alu_16_1_f_0[10]),
    .F_11(alu_16_1_f_0[11]), .F_12(alu_16_1_f_0[12]), .F_13(alu_16_1_f_0[13]), .F_14(alu_16_1_f_0[14]),
    .F_15(alu_16_1_f_0[15]));  // open: S_3, S_2, S_1, S_0, C, C0
  RAM #(.addrWidth(12), .dataWidth(16)) ram_1 (
    .addr(undriven), .din({common_bus_16_1_data_12, pc_1_p2, ar_1_p1}), .dout(ram_1_dout));  // open: we, oe, clk
  // AR ar_1: pin names not known; wires that end beside it: ar_1_p1[0], ar_1_p1[1], ar_1_p1[2], ar_1_p1[3], ar_1_p1[4], ar_1_p1[5], ar_1_p1[6]
  // PC pc_1: pin names not known; wires that end beside it: ar_1_p1[7], pc_1_p2[0], pc_1_p2[1], pc_1_p2[2], pc_1_p2[3]
  // DR dr_1: pin names not known; wires that end beside it: dr_1_p1[0], dr_1_p1[1], dr_1_p1[2], dr_1_p1[3], dr_1_p1[4], dr_1_p1[5], dr_1_p1[6], dr_1_p1[7], dr_1_p1[8], dr_1_p1[9], dr_1_p1[10]
  // ACC acc_1: pin names not known; wires that end beside it: dr_1_p1[11], dr_1_p1[12], dr_1_p1[13], dr_1_p1[14], dr_1_p1[15]
  // IR ir_1: pin names not known; wires that end beside it: ir_1_p1[0], ir_1_p1[1], ir_1_p1[2], ir_1_p1[3], ir_1_p1[4], ir_1_p1[5], ir_1_p1[6], ir_1_p1[7], ir_1_p1[8], ir_1_p1[9], ir_1_p1[10]
  // TR tr_1: pin names not known; wires that end beside it: ir_1_p1[11], ir_1_p1[12], ir_1_p1[13], ir_1_p1[14], ir_1_p1[15], tr_1_p6[0], tr_1_p6[1], tr_1_p6[2], tr_1_p6[3], tr_1_p6[4], tr_1_p6[5], tr_1_p6[6], tr_1_p6[7], tr_1_p6[8], tr_1_p6[9], tr_1_p6[10]
  // INR inr_1: pin names not known; wires that end beside it: tr_1_p6[11], tr_1_p6[12], tr_1_p6[13], tr_1_p6[14], tr_1_p6[15]
  // OUTR outr_1: pin names not known; wires that end beside it: ar_1_p1[0], ar_1_p1[1], ar_1_p1[2], ar_1_p1[3], ar_1_p1[4], ar_1_p1[5], ar_1_p1[6], ar_1_p1[7]
  COMMON_BUS_16 common_bus_16_1 (
    .A_0(ram_1_dout[0]), .A_1(ram_1_dout[1]), .A_2(ram_1_dout[2]), .A_3(ram_1_dout[3]), .A_4(ram_1_dout[4]),
    .A_5(ram_1_dout[5]), .A_6(ram_1_dout[6]), .A_7(ram_1_dout[7]), .A_8(ram_1_dout[8]), .A_9(ram_1_dout[9]),
    .A_10(ram_1_dout[10]), .A_11(ram_1_dout[11]), .A_12(ram_1_dout[12]), .A_13(ram_1_dout[13]),
    .A_14(ram_1_dout[14]), .A_15(ram_1_dout[15]), .B_0(undriven[0]), .B_1(undriven[1]), .B_2(undriven[2]),
    .B_3(undriven[3]), .B_4(undriven[4]), .B_5(undriven[5]), .B_6(undriven[6]), .B_7(undriven[7]),
    .B_8(undriven[8]), .B_9(undriven[9]), .B_10(undriven[10]), .B_11(undriven[11]), .B_12(1'b0), .B_13(1'b0),
    .B_14(1'b0), .B_15(1'b0), .C_0(undriven_2[0]), .C_1(undriven_2[1]), .C_2(undriven_2[2]),
    .C_3(undriven_2[3]), .C_4(undriven_2[4]), .C_5(undriven_2[5]), .C_6(undriven_2[6]), .C_7(undriven_2[7]),
    .C_8(undriven_2[8]), .C_9(undriven_2[9]), .C_10(undriven_2[10]), .C_11(undriven_2[11]), .C_12(1'b0),
    .C_13(1'b0), .C_14(1'b0), .C_15(1'b0), .D_0(dr_1_p1[0]), .D_1(dr_1_p1[1]), .D_2(dr_1_p1[2]),
    .D_3(dr_1_p1[3]), .D_4(dr_1_p1[4]), .D_5(dr_1_p1[5]), .D_6(dr_1_p1[6]), .D_7(dr_1_p1[7]),
    .D_8(dr_1_p1[8]), .D_9(dr_1_p1[9]), .D_10(dr_1_p1[10]), .D_11(dr_1_p1[11]), .D_12(dr_1_p1[12]),
    .D_13(dr_1_p1[13]), .D_14(dr_1_p1[14]), .D_15(dr_1_p1[15]), .E_0(undriven_3[0]), .E_1(undriven_3[1]),
    .E_2(undriven_3[2]), .E_3(undriven_3[3]), .E_4(undriven_3[4]), .E_5(undriven_3[5]), .E_6(undriven_3[6]),
    .E_7(undriven_3[7]), .E_8(undriven_3[8]), .E_9(undriven_3[9]), .E_10(undriven_3[10]),
    .E_11(undriven_3[11]), .E_12(undriven_3[12]), .E_13(undriven_3[13]), .E_14(undriven_3[14]),
    .E_15(undriven_3[15]), .F_0(ir_1_p1[0]), .F_1(ir_1_p1[1]), .F_2(ir_1_p1[2]), .F_3(ir_1_p1[3]),
    .F_4(ir_1_p1[4]), .F_5(ir_1_p1[5]), .F_6(ir_1_p1[6]), .F_7(ir_1_p1[7]), .F_8(ir_1_p1[8]),
    .F_9(ir_1_p1[9]), .F_10(ir_1_p1[10]), .F_11(ir_1_p1[11]), .F_12(ir_1_p1[12]), .F_13(ir_1_p1[13]),
    .F_14(ir_1_p1[14]), .F_15(ir_1_p1[15]), .G_0(tr_1_p6[0]), .G_1(tr_1_p6[1]), .G_2(tr_1_p6[2]),
    .G_3(tr_1_p6[3]), .G_4(tr_1_p6[4]), .G_5(tr_1_p6[5]), .G_6(tr_1_p6[6]), .G_7(tr_1_p6[7]),
    .G_8(tr_1_p6[8]), .G_9(tr_1_p6[9]), .G_10(tr_1_p6[10]), .G_11(tr_1_p6[11]), .G_12(tr_1_p6[12]),
    .G_13(tr_1_p6[13]), .G_14(tr_1_p6[14]), .G_15(tr_1_p6[15]), .H_0(undriven_4[0]), .H_1(undriven_4[1]),
    .H_2(undriven_4[2]), .H_3(undriven_4[3]), .H_4(undriven_4[4]), .H_5(undriven_4[5]), .H_6(undriven_4[6]),
    .H_7(undriven_4[7]), .H_8(1'b0), .H_9(1'b0), .H_10(1'b0), .H_11(1'b0), .H_12(1'b0), .H_13(1'b0),
    .H_14(1'b0), .H_15(1'b0), .DATA_0(ar_1_p1[0]), .DATA_1(ar_1_p1[1]), .DATA_2(ar_1_p1[2]),
    .DATA_3(ar_1_p1[3]), .DATA_4(ar_1_p1[4]), .DATA_5(ar_1_p1[5]), .DATA_6(ar_1_p1[6]), .DATA_7(ar_1_p1[7]),
    .DATA_8(pc_1_p2[0]), .DATA_9(pc_1_p2[1]), .DATA_10(pc_1_p2[2]), .DATA_11(pc_1_p2[3]),
    .DATA_12(common_bus_16_1_data_12[0]), .DATA_13(common_bus_16_1_data_12[1]),
    .DATA_14(common_bus_16_1_data_12[2]), .DATA_15(common_bus_16_1_data_12[3]));  // open: S_2, S_1, S_0
endmodule
